# Fritzing sketch wirc-bb (saved by Fritzing 0.9.3b)
breadboards: 1

parts:
  LED1 = LED - 5mm [color="Infrared (940nm)" package="5 mm [THT]"]
  R1 = Resistor [tolerance=±5% resistance=150 package=THT]
  WeMos_D1_Mini1 = WeMos D1 Mini  # not connected

nets:
  N1: LED1.anode, R1.Pin_0
